# Fritzing sketch PCB_v1 (saved by Fritzing 0.9.3b)
circuit board: 9.71298cm x 5.37789cm

parts:
  부품1 = Arduino Nano (Rev3.0)
  부품2 = Motor Driver 1A Dual TB6612FNG
  부품3 = Motor Driver 1A Dual TB6612FNG
  J1 = female pin header, 6 pins [form="♀ (female)"]
  J2 = female pin header, 6 pins [form="♀ (female)"]
  J3 = female pin header, 6 pins [form="♀ (female)"]
  J4 = female pin header, 6 pins [form="♀ (female)"]
  Power_plug_12V = Power plug
  Power_plug_5V = Power plug
  J5 = female pin header, 2 pins [form="♀ (female)"]

nets:
  N1: 부품1.D1/TX, 부품2.AIN1
  N2: 부품1.D0/RX, 부품2.AIN2
  GND: 부품1.GND, 부품2.GND, 부품3.GND, J1.pin4, J2.pin4, J3.pin4, J4.pin4, Power_plug_12V.GND, Power_plug_5V.GND
  N3: 부품1.D2, J3.pin1
  N4: 부품1.D3, J4.pin1
  N5: 부품1.D4, 부품2.BIN1
  N6: 부품1.D5, 부품2.PWMA
  N7: 부품1.D6, 부품2.PWMB
  N8: 부품1.D7, 부품2.BIN2
  N9: 부품1.D8, 부품3.AIN1
  N10: 부품1.D9, 부품3.PWMA
  N11: 부품1.D10, 부품3.PWMB
  N12: 부품1.D11/MOSI, 부품3.AIN2
  N13: 부품1.D12/MISO, 부품3.BIN1
  VCC: 부품1.VIN, 부품2.VCC, 부품2.STBY, 부품3.VCC, 부품3.STBY, J1.pin3, J2.pin3, J3.pin3, J4.pin3, Power_plug_5V.VCC
  N14: 부품1.A7, J4.pin2
  N15: 부품1.A6, J3.pin2
  N16: 부품1.A5, J5.pin2
  N17: 부품1.A4, J5.pin1
  N18: 부품1.A3, J2.pin1
  N19: 부품1.A2, J1.pin1
  N20: 부품1.A1, J2.pin2
  N21: 부품1.A0, J1.pin2
  N22: 부품1.D13/SCK, 부품3.BIN2
  N23: 부품2.B01, J2.pin5
  N24: 부품2.B02, J2.pin6
  N25: 부품2.A02, J1.pin6
  N26: 부품2.A01, J1.pin5
  N27: 부품2.VM, 부품3.VM, Power_plug_12V.VCC
  N28: 부품3.B01, J4.pin5
  N29: 부품3.B02, J4.pin6
  N30: 부품3.A02, J3.pin6
  N31: 부품3.A01, J3.pin5
