# Fritzing sketch ver2 (saved by Fritzing 0.9.3b)
circuit board: 8cm x 8cm

parts:
  1st_MotorDriver = Motor Driver 1A Dual TB6612FNG
  Slave_Nano = Arduino Nano (Rev3.0)
  CapSense = female pin header, 4 pins [form="♀ (female)"]
  J3 = female pin header, 2 pins [form="♀ (female)"]
  J4 = female pin header, 2 pins [form="♀ (female)"]
  J5 = female pin header, 2 pins [form="♀ (female)"]
  J6 = female pin header, 2 pins [form="♀ (female)"]
  2nd_MotorDriver = Motor Driver 1A Dual TB6612FNG
  Power_plug2 = Power plug
  Power_plug3 = Power plug
  I2C = female pin header, 2 pins [form="♀ (female)"]
  GND = female pin header, 4 pins [form="♀ (female)"]
  5V = female pin header, 4 pins [form="♀ (female)"]
  Pos = female pin header, 4 pins [form="♀ (female)"]

nets (from the pcb view):
  N1: 1st_MotorDriver.B01, J4.pin2
  N2: 1st_MotorDriver.B02, J4.pin1
  N3: 1st_MotorDriver.A02, J3.pin1
  N4: 1st_MotorDriver.A01, J3.pin2
  GND: 1st_MotorDriver.GND, Slave_Nano.GND, 2nd_MotorDriver.GND, Power_plug2.GND, Power_plug3.GND, GND.pin1, GND.pin2, GND.pin3, GND.pin4
  VCC: 1st_MotorDriver.VCC, 1st_MotorDriver.STBY, Slave_Nano.VIN, 2nd_MotorDriver.VCC, 2nd_MotorDriver.STBY, Power_plug2.VCC, 5V.pin1, 5V.pin2, 5V.pin3, 5V.pin4
  N5: 1st_MotorDriver.VM, 2nd_MotorDriver.VM, Power_plug3.VCC
  N6: 1st_MotorDriver.PWMA, Slave_Nano.D9
  N7: 1st_MotorDriver.AIN2, Slave_Nano.A7
  N8: 1st_MotorDriver.AIN1, Slave_Nano.A6
  N9: 1st_MotorDriver.BIN1, Slave_Nano.D1/TX
  N10: 1st_MotorDriver.BIN2, Slave_Nano.D0/RX
  N11: 1st_MotorDriver.PWMB, Slave_Nano.D6
  N12: Slave_Nano.D2, CapSense.pin4
  N13: Slave_Nano.D3, CapSense.pin3
  N14: Slave_Nano.D4, CapSense.pin2
  N15: Slave_Nano.D5, CapSense.pin1
  N16: Slave_Nano.D7, 2nd_MotorDriver.BIN1
  N17: Slave_Nano.D8, 2nd_MotorDriver.AIN1
  N18: Slave_Nano.D10, 2nd_MotorDriver.PWMB
  N19: Slave_Nano.D11/MOSI, 2nd_MotorDriver.PWMA
  N20: Slave_Nano.D12/MISO, 2nd_MotorDriver.AIN2
  N21: Slave_Nano.A5, I2C.pin1
  N22: Slave_Nano.A4, I2C.pin2
  N23: Slave_Nano.A3, Pos.pin4
  N24: Slave_Nano.A2, Pos.pin3
  N25: Slave_Nano.A1, Pos.pin2
  N26: Slave_Nano.A0, Pos.pin1
  N27: Slave_Nano.D13/SCK, 2nd_MotorDriver.BIN2
  N28: J5.pin1, 2nd_MotorDriver.A02
  N29: J5.pin2, 2nd_MotorDriver.A01
  N30: J6.pin1, 2nd_MotorDriver.B02
  N31: J6.pin2, 2nd_MotorDriver.B01
