# Fritzing sketch ver3 (saved by Fritzing 0.9.3b)
circuit board: 8cm x 8cm
breadboards: 1

parts:
  1st_MotorDriver1 = Motor Driver 1A Dual TB6612FNG
  2nd_MotorDriver1 = Motor Driver 1A Dual TB6612FNG
  Pos1 = female pin header, 4 pins [form="♀ (female)"]
  I2C1 = female pin header, 2 pins [form="♀ (female)"]
  J7 = female pin header, 2 pins [form="♀ (female)"]
  J8 = female pin header, 2 pins [form="♀ (female)"]
  J9 = female pin header, 2 pins [form="♀ (female)"]
  J10 = female pin header, 2 pins [form="♀ (female)"]
  Power_plug4 = Power plug
  Power_plug5 = Power plug
  Slave_Nano1 = Arduino Nano (Rev3.0)
  5V2 = female pin header, 4 pins [form="♀ (female)"]
  5V3 = female pin header, 4 pins [form="♀ (female)"]
  5V4 = female pin header, 4 pins [form="♀ (female)"]

nets:
  GND: 1st_MotorDriver1.GND, 2nd_MotorDriver1.GND, Power_plug4.GND, Power_plug5.GND, Slave_Nano1.GND, 5V2.pin1, 5V2.pin2, 5V2.pin3, 5V2.pin4
  N1: 1st_MotorDriver1.B01, J10.pin2
  N2: 1st_MotorDriver1.B02, J10.pin1
  N3: 1st_MotorDriver1.A02, J9.pin1
  N4: 1st_MotorDriver1.A01, J9.pin2
  VCC: 1st_MotorDriver1.VCC, 1st_MotorDriver1.STBY, 2nd_MotorDriver1.VCC, 2nd_MotorDriver1.STBY, Power_plug5.VCC, Slave_Nano1.VIN, 5V4.pin1, 5V4.pin2, 5V4.pin3, 5V4.pin4
  N5: 1st_MotorDriver1.VM, 2nd_MotorDriver1.VM, Power_plug4.VCC
  N6: 1st_MotorDriver1.PWMA, Slave_Nano1.D6
  N7: 1st_MotorDriver1.AIN2, Slave_Nano1.D13/SCK
  N8: 1st_MotorDriver1.AIN1, Slave_Nano1.D12/MISO
  N9: 1st_MotorDriver1.BIN1, Slave_Nano1.D9
  N10: 1st_MotorDriver1.BIN2, Slave_Nano1.D10
  N11: 1st_MotorDriver1.PWMB, Slave_Nano1.D11/MOSI
  N12: 2nd_MotorDriver1.B01, J8.pin2
  N13: 2nd_MotorDriver1.B02, J8.pin1
  N14: 2nd_MotorDriver1.A02, J7.pin1
  N15: 2nd_MotorDriver1.A01, J7.pin2
  N16: 2nd_MotorDriver1.PWMA, Slave_Nano1.D3
  N17: 2nd_MotorDriver1.AIN2, Slave_Nano1.D1/TX
  N18: 2nd_MotorDriver1.AIN1, Slave_Nano1.D0/RX
  N19: 2nd_MotorDriver1.BIN1, Slave_Nano1.D2
  N20: 2nd_MotorDriver1.BIN2, Slave_Nano1.D4
  N21: 2nd_MotorDriver1.PWMB, Slave_Nano1.D5
  N22: Pos1.pin1, Slave_Nano1.A2
  N23: Pos1.pin2, Slave_Nano1.A3
  N24: Pos1.pin3, Slave_Nano1.A6
  N25: Pos1.pin4, Slave_Nano1.A7
  N26: I2C1.pin1, Slave_Nano1.A5
  N27: I2C1.pin2, Slave_Nano1.A4
  N28: Slave_Nano1.D7, 5V3.pin4
  N29: Slave_Nano1.D8, 5V3.pin3
  N30: Slave_Nano1.A1, 5V3.pin1
  N31: Slave_Nano1.A0, 5V3.pin2
