# Fritzing sketch ver5 (saved by Fritzing 0.9.3b)

parts:
  2nd_MotorDriver3 = Motor Driver 1A Dual TB6612FNG
  2nd_MotorDriver4 = Motor Driver 1A Dual TB6612FNG
  Slave_Nano1 = Arduino Nano (Rev3.0)
  DC_9~12V1 = Power plug
  DC_5V1 = Power plug
  OUT2 = female pin header, 4 pins [form="♀ (female)"]
  OUT3 = female pin header, 4 pins [form="♀ (female)"]
  OUT4 = female pin header, 4 pins [form="♀ (female)"]
  I2C1 = female pin header, 2 pins [form="♀ (female)"]
  OUT5 = female pin header, 4 pins [form="♀ (female)"]

nets:
  GND: 2nd_MotorDriver3.GND, 2nd_MotorDriver4.GND, Slave_Nano1.GND, DC_9~12V1.GND, DC_5V1.GND
  N1: 2nd_MotorDriver3.B01, OUT3.pin4
  N2: 2nd_MotorDriver3.B02, OUT3.pin3
  N3: 2nd_MotorDriver3.A02, OUT3.pin2
  N4: 2nd_MotorDriver3.A01, OUT3.pin1
  VCC: 2nd_MotorDriver3.VCC, 2nd_MotorDriver3.STBY, 2nd_MotorDriver4.VCC, 2nd_MotorDriver4.STBY, Slave_Nano1.VIN, DC_5V1.VCC
  N5: 2nd_MotorDriver3.VM, 2nd_MotorDriver4.VM, DC_9~12V1.VCC
  N6: 2nd_MotorDriver3.PWMA, Slave_Nano1.D3
  N7: 2nd_MotorDriver3.AIN2, Slave_Nano1.D1/TX
  N8: 2nd_MotorDriver3.AIN1, Slave_Nano1.D0/RX
  N9: 2nd_MotorDriver3.BIN1, Slave_Nano1.D2
  N10: 2nd_MotorDriver3.BIN2, Slave_Nano1.D4
  N11: 2nd_MotorDriver3.PWMB, Slave_Nano1.D5
  N12: 2nd_MotorDriver4.B01, OUT4.pin4
  N13: 2nd_MotorDriver4.B02, OUT4.pin3
  N14: 2nd_MotorDriver4.A02, OUT4.pin2
  N15: 2nd_MotorDriver4.A01, OUT4.pin1
  N16: 2nd_MotorDriver4.PWMA, Slave_Nano1.D6
  N17: 2nd_MotorDriver4.AIN2, Slave_Nano1.D13/SCK
  N18: 2nd_MotorDriver4.AIN1, Slave_Nano1.D12/MISO
  N19: 2nd_MotorDriver4.BIN1, Slave_Nano1.D9
  N20: 2nd_MotorDriver4.BIN2, Slave_Nano1.D10
  N21: 2nd_MotorDriver4.PWMB, Slave_Nano1.D11/MOSI
  N22: Slave_Nano1.D7, OUT5.pin1
  N23: Slave_Nano1.D8, OUT5.pin2
  N24: Slave_Nano1.A7, OUT2.pin4
  N25: Slave_Nano1.A6, OUT2.pin3
  N26: Slave_Nano1.A5, I2C1.pin2
  N27: Slave_Nano1.A4, I2C1.pin1
  N28: Slave_Nano1.A3, OUT2.pin2
  N29: Slave_Nano1.A2, OUT2.pin1
  N30: Slave_Nano1.A1, OUT5.pin4
  N31: Slave_Nano1.A0, OUT5.pin3
